# Fritzing sketch Schematics (saved by Fritzing 0.9.3b)

parts:
  U1 = WS2812 RGB LED strip
  U2 = WS2812 RGB LED strip
  U3 = WS2812 RGB LED strip
  JACK1 = 2.1mm Barrel Jack with Terminal Block
  R1 = Resistor [tolerance=±5% resistance=220 package=THT]
  R2 = Resistor [tolerance=±5% resistance=220 package=THT]
  R3 = Resistor [tolerance=±5% resistance=220 package=THT]

nets:
  GND: U1.GND, U2.GND, U3.GND, JACK1.NEG
  VCC: U1.VCC, U2.VCC, U3.VCC, JACK1.POS
  N1: U1.DIN, R2.Pin_1
  N2: U2.DIN, R3.Pin_1
  N3: U3.DIN, R1.Pin_1

notes:
  Led Set 2
  Led Set 3
  Led Set 1
  330 Ohm Resistor
  5V External Power Supply
  SEEED NRF52 Board
  Android Phone
  Pin D1
  Pin D2
  Pin D3

custom parts:
  WS2812 RGB LED strip: WS2812 strip
